// Logisim project LR_LATCH.circ as structural Verilog: 2 circuits, main circuit main
module main (
  input  in_1,
  input  in_2
);

  wire and_1_out, not_1_out, or_1_out;

  or or_1 (or_1_out, and_1_out, in_1);
  not not_1 (not_1_out, in_2);
  and and_1 (and_1_out, or_1_out, not_1_out);
  LED led_1 (.in(and_1_out));
endmodule

module SET_RESET (
  input  in_1,
  input  in_2,
  output out_3
);

  wire not_1_out, or_1_out;

  or or_1 (or_1_out, out_3, in_1);
  not not_1 (not_1_out, in_2);
  and and_1 (out_3, or_1_out, not_1_out);
endmodule
